# Fritzing sketch HW_2_Asli_Gozde (saved by Fritzing 1.0.3b)
breadboards: 1

parts:
  J1 = STM32 Nucleo boards
  R1 = Resistor [tolerance=±5% power=0.25W resistance=330 package=THT]
  R2 = Resistor [tolerance=±5% power=0.25W resistance=330 package=THT]
  R3 = Resistor [tolerance=±5% power=0.25W resistance=330 package=THT]
  R4 = Resistor [tolerance=±5% power=0.25W resistance=330 package=THT]
  R5 = Resistor [tolerance=±5% power=0.25W resistance=330 package=THT]
  R6 = Resistor [tolerance=±5% power=0.25W resistance=330 package=THT]
  R7 = Resistor [tolerance=±5% power=0.25W resistance=330 package=THT]
  R8 = Resistor [tolerance=±5% power=0.25W resistance=330 package=THT]
  R9 = Resistor [tolerance=±5% power=0.25W resistance=330 package=THT]
  S1 = Pushbutton [package="[THT]"]
  S2 = Pushbutton [package="[THT]"]
  DI1 = 7-Segment LED Display [package=THT]

nets:
  N1: J1.A0, R7.Pin_1
  N2: J1.A1, R9.Pin_1
  N3: J1.A2, R5.Pin_1
  N4: J1.D8, R1.Pin_1
  N5: J1.D11_PWM/MOSI, R6.Pin_0
  N6: J1.D12/MISO, R3.Pin_0
  N7: J1.D13/SCK, R4.Pin_0
  N8: J1.A4/SDA, S1.Pin_3, S1.Pin_4
  N9: J1.A5/SCL, S2.Pin_3, S2.Pin_4
  N10: J1.D7, R8.Pin_0
  N11: J1.3V3, R2.Pin_0
  N12: J1.GND, S1.Pin_1, S1.Pin_2, S2.Pin_1, S2.Pin_2
  N13: R1.Pin_0, DI1.cathodeDP
  N14: R2.Pin_1, DI1.commAnode#2
  N15: R3.Pin_1, DI1.cathodeE
  N16: R4.Pin_1, DI1.cathodeD
  N17: R5.Pin_0, DI1.cathodeC
  N18: R6.Pin_1, DI1.cathodeF
  N19: R7.Pin_0, DI1.cathodeA
  N20: R8.Pin_1, DI1.cathodeG
  N21: R9.Pin_0, DI1.cathodeB
